# Fritzing sketch Untitled Sketch (saved by Fritzing 0.9.4)
circuit board: 6.88566cm x 5.36311cm
breadboards: 1

parts:
  Lora_E32 = ossoyoo-lora-module  # not connected
  TXD = Header 1 [package=1x01_offset]
  RXD = Header 1 [package=1x01_offset]
  M0 = Header 1 [package=1x01_offset]
  M1 = Header 1 [package=1x01_offset]
  GND = Header 1 [package=1x01_offset]
  AUX = Header 1 [package=1x01_offset]
  VCC = Header 1 [package=1x01_offset]
  arduino_uno = Arduino Uno (Rev3) - ICSP
  220 = Resistor [tolerance=±5% resistance=220 package=THT]
  reset = Pushbutton [package=THT]

nets (from the pcb view):
  N1: TXD.1, arduino_uno.D7
  N2: RXD.1, arduino_uno.D8
  N3: M0.1, arduino_uno.D10_PWM/SS
  N4: M1.1, arduino_uno.D9_PWM
  N5: GND.1, arduino_uno.GND
  N6: AUX.1, arduino_uno.D6_PWM
  N7: VCC.1, arduino_uno.5V, 220.Pin_0, reset.leg0
  N8: arduino_uno.RESET2, reset.leg1

custom parts:
  ossoyoo-lora-module: Osoyoo Long Distance wireless transceiver Uart LoRa Module.

// code stored in the sketch: essefunciona.ino
/*
 * LoRa E32-TTL-100
 * Start device, reset or write to the Serial to send a message.
 * https://www.mischianti.org/2019/10/15/lora-e32-device-for-arduino-esp32-or-esp8266-specs-and-basic-usage-part-1/
 *
 * E32-TTL-100----- Arduino UNO
 * M0         ----- GND
 * M1         ----- GND
 * TX         ----- PIN 2 (PullUP)
 * RX         ----- PIN 3 (PullUP & Voltage divider)
 * AUX        ----- Not connected
 * VCC        ----- 3.3v/5v
 * GND        ----- GND
 *
 */
#include "Arduino.h"
#include "LoRa_E32.h"

// ---------- Arduino pins --------------
LoRa_E32 e32ttl(2, 3, 5, 7, 6);
//LoRa_E32 e32ttl100(2, 3); // Config without connect AUX and M0 M1

//#include <SoftwareSerial.h>
//SoftwareSerial mySerial(2, 3);  // e32 TX e32 RX
//LoRa_E32 e32ttl(&mySerial, 5, 7, 6);
// -------------------------------------

void setup() {
  Serial.begin(9600);
  delay(500);

  // Startup all pins and UART
  e32ttl.begin();

ResponseStructContainer c;
  c = e32ttl.getConfiguration();
  // It's important get configuration pointer before all other operation
  Configuration configuration = *(Configuration*) c.data;
  Serial.println(c.status.getResponseDescription());
  Serial.println(c.status.code);

  printParameters(configuration);

  ResponseStructContainer cMi;
  cMi = e32ttl.getModuleInformation();
  // It's important get information pointer before all other operation
  ModuleInformation mi = *(ModuleInformation*)cMi.data;

  Serial.println(cMi.status.getResponseDescription());
  Serial.println(cMi.status.code);

  printModuleInformation(mi);

  c.close();
  cMi.close();

  Serial.println("Hi, I'm going to send message!");
}

void loop() {
	// If something available
  if (e32ttl.available()>1) {
	  // read the String message
	ResponseContainer rc = e32ttl.receiveMessage();
	// Is something goes wrong print error
	if (rc.status.code!=1){
		rc.status.getResponseDescription();
	}else{
		// Print the data received
		Serial.println(rc);
	}
  }
  if (Serial.available()) {
	  String input = Serial.readString();
	  e32ttl.sendMessage(input);
  }

//  ResponseStatus rs =

}

void printParameters(struct Configuration configuration) {
  Serial.println("----------------------------------------");

  Serial.print(F("HEAD BIN: "));  Serial.print(configuration.HEAD, BIN);Serial.print(" ");Serial.print(configuration.HEAD, DEC);Serial.print(" ");Serial.println(configuration.HEAD, HEX);
  Serial.println(F(" "));
  Serial.print(F("AddH BIN: "));  Serial.println(configuration.ADDH, BIN);
  Serial.print(F("AddL BIN: "));  Serial.println(configuration.ADDL, BIN);
  Serial.print(F("Chan BIN: "));  Serial.print(configuration.CHAN, DEC); Serial.print(" -> "); Serial.println(configuration.getChannelDescription());
  Serial.println(F(" "));
  Serial.print(F("SpeedParityBit BIN    : "));  Serial.print(configuration.SPED.uartParity, BIN);Serial.print(" -> "); Serial.println(configuration.SPED.getUARTParityDescription());
  Serial.print(F("SpeedUARTDataRate BIN : "));  Serial.print(configuration.SPED.uartBaudRate, BIN);Serial.print(" -> "); Serial.println(configuration.SPED.getUARTBaudRate());
  Serial.print(F("SpeedAirDataRate BIN  : "));  Serial.print(configuration.SPED.airDataRate, BIN);Serial.print(" -> "); Serial.println(configuration.SPED.getAirDataRate());

  Serial.print(F("OptionTrans BIN       : "));  Serial.print(configuration.OPTION.fixedTransmission, BIN);Serial.print(" -> "); Serial.println(configuration.OPTION.getFixedTransmissionDescription());
  Serial.print(F("OptionPullup BIN      : "));  Serial.print(configuration.OPTION.ioDriveMode, BIN);Serial.print(" -> "); Serial.println(configuration.OPTION.getIODroveModeDescription());
  Serial.print(F("OptionWakeup BIN      : "));  Serial.print(configuration.OPTION.wirelessWakeupTime, BIN);Serial.print(" -> "); Serial.println(configuration.OPTION.getWirelessWakeUPTimeDescription());
  Serial.print(F("OptionFEC BIN         : "));  Serial.print(configuration.OPTION.fec, BIN);Serial.print(" -> "); Serial.println(configuration.OPTION.getFECDescription());
  Serial.print(F("OptionPower BIN       : "));  Serial.print(configuration.OPTION.transmissionPower, BIN);Serial.print(" -> "); Serial.println(configuration.OPTION.getTransmissionPowerDescription());

  Serial.println("----------------------------------------");

}
void printModuleInformation(struct ModuleInformation moduleInformation) {
  Serial.println("----------------------------------------");
  Serial.print(F("HEAD BIN: "));  Serial.print(moduleInformation.HEAD, BIN);Serial.print(" ");Serial.print(moduleInformation.HEAD, DEC);Serial.print(" ");Serial.println(moduleInformation.HEAD, HEX);

  Serial.print(F("Freq.: "));  Serial.println(moduleInformation.frequency, HEX);
  Serial.print(F("Version  : "));  Serial.println(moduleInformation.version, HEX);
  Serial.print(F("Features : "));  Serial.println(moduleInformation.features, HEX);
  Serial.println("----------------------------------------");

}
